# Fritzing sketch derdiedas_diagram (saved by Fritzing 0.9.3b)
breadboards: 1

parts:
  Part1 = Arduino Uno (Rev3)
  S1 = Pushbutton [package="[THT]"]
  S2 = Pushbutton [package="[THT]"]
  S3 = Pushbutton [package="[THT]"]
  LCD1 = LCD screen  # not connected

nets:
  N1: Part1.5V, S1.Pin_1, S1.Pin_2, S2.Pin_1, S2.Pin_2, S3.Pin_1, S3.Pin_2
  N2: S1.Pin_3, S1.Pin_4
  N3: S2.Pin_3, S2.Pin_4
  N4: S3.Pin_3, S3.Pin_4
